# Fritzing sketch TiltBallAdapter (saved by Fritzing 0.7.10b)

parts:
  J1 = female pin header, 3 pins [form="♀ (female)"]
  J2 = female pin header, 3 pins [form="♀ (female)"]

nets:
  N1: J1.pin1, J2.pin3
  N2: J1.pin2, J2.pin2
  N3: J1.pin3, J2.pin1
